# Fritzing sketch distance and rgb (saved by Fritzing 0.9.4)
breadboards: 1

parts:
  Part1 = Arduino Mega 2560 (Rev3)
  HC-SR04_Sensor_1 = HC-SR04 Ultrasonic Distance Sensor
  R1 = Resistor [tolerance=±5% resistance=220 package=THT]
  R2 = Resistor [tolerance=±5% resistance=220 package=THT]
  R3 = Resistor [tolerance=±5% resistance=220 package=THT]
  LED1 = RGB LED (com. cathode, rbg) [package="5 mm [THT]"]

nets:
  GND: Part1.GND, HC-SR04_Sensor_1.GND, LED1.common_cathode
  N1: Part1.D10_PWM, R1.Pin_0
  N2: Part1.D9_PWM, R2.Pin_0
  N3: Part1.D8_PWM, R3.Pin_0
  5V: Part1.5V, HC-SR04_Sensor_1.VCC
  N4: Part1.D5_PWM, HC-SR04_Sensor_1.TRIG
  N5: Part1.D6_PWM, HC-SR04_Sensor_1.ECHO
  N6: R1.Pin_1, LED1.green_anode
  N7: R2.Pin_1, LED1.blue_anode
  N8: R3.Pin_1, LED1.red_anode
