# Fritzing sketch IR Receiver and LCD circuit (saved by Fritzing 0.9.4)
breadboards: 1

parts:
  16x2_LCD_(liquid_crystal_display) = LCD screen
  Arduino_Mega_2560 = Arduino Mega 2560 (Rev3)
  10k_potentiometer = Trimmer Potentiometer [maximum_resistance=10kΩ package=THT]
  IR_receiver = KY-022 Infrared Receiver Module [package="Breakout board"]

nets:
  VSS: 16x2_LCD_(liquid_crystal_display).VSS, 16x2_LCD_(liquid_crystal_display).R/W, 16x2_LCD_(liquid_crystal_display).LED-, Arduino_Mega_2560.GND, 10k_potentiometer.leg1, IR_receiver.-
  VDD: 16x2_LCD_(liquid_crystal_display).VDD, 16x2_LCD_(liquid_crystal_display).LED+, Arduino_Mega_2560.5V, IR_receiver.Vin
  N1: 16x2_LCD_(liquid_crystal_display).V0, 10k_potentiometer.wiper
  N2: 16x2_LCD_(liquid_crystal_display).RS, Arduino_Mega_2560.D3_PWM
  N3: 16x2_LCD_(liquid_crystal_display).E, Arduino_Mega_2560.D4_PWM
  N4: 16x2_LCD_(liquid_crystal_display).DB4, Arduino_Mega_2560.D5_PWM
  N5: 16x2_LCD_(liquid_crystal_display).DB5, Arduino_Mega_2560.D6_PWM
  N6: 16x2_LCD_(liquid_crystal_display).DB6, Arduino_Mega_2560.D7_PWM
  N7: 16x2_LCD_(liquid_crystal_display).DB7, Arduino_Mega_2560.D8_PWM
  N8: Arduino_Mega_2560.D2_PWM, IR_receiver.S

custom parts:
  KY-022 Infrared Receiver Module: Arduino IR receiver module KY-022, based on 1838 IR Receiver/Decoder. It reacts to 38kHz infrared light.
