# Fritzing sketch IR remote and RGB LED (saved by Fritzing 0.9.4)
breadboards: 1

parts:
  Part1 = Arduino Mega 2560 (Rev3)
  R1 = Resistor [tolerance=±5% resistance=220 package=THT]
  R2 = Resistor [tolerance=±5% resistance=220 package=THT]
  R3 = Resistor [tolerance=±5% resistance=220 package=THT]
  LED1 = RGB LED (com. cathode, rbg) [package="5 mm [THT]"]
  Mod1 = KY-022 Infrared Receiver Module [package="Breakout board"]

nets:
  N1: Part1.GND, LED1.common_cathode, Mod1.-
  N2: Part1.D10_PWM, R1.Pin_0
  N3: Part1.D9_PWM, R2.Pin_0
  N4: Part1.D8_PWM, R3.Pin_0
  5V: Part1.5V, Mod1.Vin
  N5: Part1.D2_PWM, Mod1.S
  N6: R1.Pin_1, LED1.green_anode
  N7: R2.Pin_1, LED1.blue_anode
  N8: R3.Pin_1, LED1.red_anode

custom parts:
  KY-022 Infrared Receiver Module: KY-022 IR receiver module, reacts to 38kHz infrared light.
