# Fritzing sketch Robot kit motor wiring (saved by Fritzing 0.9.4)
breadboards: 1

parts:
  Part1 = Arduino Mega 2560 (Rev3)
  IC1 = L293D [package=THT]
  BAT1 = Battery Holders [package=battery-aa-panel]

nets:
  N1: Part1.D17_PWM/RX2, IC1.In_3
  N2: Part1.D16_PWM/TX2, IC1.In_4
  N3: Part1.D15/RX3, IC1.Enable_2
  N4: Part1.5V, IC1.+V
  N5: Part1.GND, IC1.0V, BAT1.-
  N6: Part1.D4_PWM, IC1.In_1
  N7: Part1.D5_PWM, IC1.In_2
  N8: Part1.D6_PWM, IC1.Enable_1
  N9: IC1.+Vmotor, BAT1.+

notes:
  Right ("passenger side") NXT servo cable
  Left ("driver side") NXT servo cable
  The +9V wire from the 6 AA battery pack DOES NOT connect to the usual + rails on the breadboard.
  The "-" or "GND" wire from the 6 AA battery pack DOES connect to the usual - rails on the breadboard.
  Arduino pins:
  2 Left NXT yellow wire (Tacho1)
  3 Left NXT blue wire (Tacho2)
  4 L293D pin 2 (left motor control direction 1)
  5 L293D pin 7 (left motor control direction 2)
  6 L293D pin 1 (left motor enable)
  15 L293D pin 9 (right motor enable)
  16 L293D pin 15 (right motor control direction 2)
  17 L293D pin 10 (right motor control direction 1)
  18 Right NXT yellow wire (Tacho1)
  19 Right NXT blue wire (Tacho2)
  +5V to breadboard + rail
  GND to breadboard - rail
